# Fritzing sketch robot (saved by Fritzing 0.9.3b)

parts:
  Часть1 = Arduino Uno (Rev3)
  Часть5 = Arduino Cellular Shield
  M8 = DC Motor
  M9 = DC Motor
  M10 = DC Motor
  M11 = DC Motor
  M12 = DC Motor
  M13 = DC Motor
  VCC3 = Battery
  L298N1 = L298N DC motor driver
  L298N2 = L298N DC motor driver
  L298N3 = L298N DC motor driver
  PWM1 = PCA9685 16x12-bit PWM Breakout

nets:
  N1: Часть1.A4/SDA, PWM1.no_name_yet#504
  N2: Часть1.A5/SCL, PWM1.no_name_yet#503
  N3: Часть1.GND, PWM1.no_name_yet#501
  N4: Часть1.D0/RX, Часть5.RX-I
  N5: Часть1.D1/TX, Часть5.TX-O
  N6: Часть1.5V, PWM1.no_name_yet#505
  N7: M8.pin_1, L298N1.OUT2
  N8: M8.pin_2, L298N1.OUT1
  N9: M9.pin_1, L298N1.OUT4
  N10: M9.pin_2, L298N1.OUT3
  N11: M10.pin_1, L298N2.OUT2
  N12: M10.pin_2, L298N2.OUT1
  N13: M11.pin_1, L298N2.OUT4
  N14: M11.pin_2, L298N2.OUT3
  N15: M12.pin_1, L298N3.OUT2
  N16: M12.pin_2, L298N3.OUT1
  N17: M13.pin_1, L298N3.OUT4
  N18: M13.pin_2, L298N3.OUT3
  GND: VCC3.-, L298N1.GND, L298N2.GND, L298N3.GND
  12V: VCC3.+, L298N1.12V, L298N2.12V, L298N3.12V
  N19: L298N1.ENA, PWM1.no_name_yet#15
  N20: L298N1.ENB, PWM1.no_name_yet#12
  N21: L298N1.IN2, PWM1.no_name_yet#14
  N22: L298N1.IN3, PWM1.no_name_yet#13
  N23: L298N2.ENA, PWM1.no_name_yet#11
  N24: L298N2.ENB, PWM1.no_name_yet#8
  N25: L298N2.IN2, PWM1.no_name_yet#10
  N26: L298N2.IN3, PWM1.no_name_yet#9
  N27: L298N3.ENA, PWM1.no_name_yet#7
  N28: L298N3.ENB, PWM1.no_name_yet#4
  N29: L298N3.IN2, PWM1.no_name_yet#6
  N30: L298N3.IN3, PWM1.no_name_yet#5

custom parts:
  L298N DC motor driver: 2x DC motor driver with 78M05 positive voltage regulator (7..35 V) L298N: max 46 V, 2 A Set 5 V Enable jumper to enable 5 V regultor (needed for the L298N) and +5 V output at screw terminal or supply external +5 V at screw terminal Set ENA and/or ENB to +5 V to enable motor permanently or supply ENA and/or ENB with PWM signal IN1 and IN2 set rotation directory for motor A (OUT1/OUT2) IN2 and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
